# Fritzing sketch Practica#1_PuertoParalelo (saved by Fritzing 0.9.4)
breadboards: 1

parts:
  DI1 = 7-Segment LED Display [package=THT]
  SW1 = DIP Switch 8 Position [package=dipswitch-08]
  IC1 = IC, DIP package, 20 pins [chip_label=SN74LS374]
  R1 = Resistor [tolerance=±5% resistance=220 package="0805 [SMD]"]
  R2 = Resistor [tolerance=±5% resistance=220 package="0805 [SMD]"]
  R3 = Resistor [tolerance=±5% resistance=220 package="0805 [SMD]"]
  R4 = Resistor [tolerance=±5% resistance=220 package="0805 [SMD]"]
  R5 = Resistor [tolerance=±5% resistance=220 package="0805 [SMD]"]
  R6 = Resistor [tolerance=±5% resistance=220 package="0805 [SMD]"]
  R7 = Resistor [tolerance=±5% resistance=220 package="0805 [SMD]"]
  R8 = Resistor [tolerance=±5% resistance=220 package="0805 [SMD]"]
  R9 = Resistor [tolerance=±5% resistance=220 package="0805 [SMD]"]
  X1 = F25 [package=db25]
  IC2 = IC, DIP package, 16 pins [chip_label=SN74LS157]

nets:
  N1: DI1.cathodeE, IC1.pin12
  N2: DI1.cathodeD, IC1.pin9
  N3: DI1.commAnode#2, R1.Pin_0
  N4: DI1.cathodeC, IC1.pin6
  N5: DI1.cathodeDP, IC1.pin19
  N6: DI1.cathodeB, IC1.pin5
  N7: DI1.cathodeA, IC1.pin2
  N8: DI1.cathodeF, IC1.pin16
  N9: DI1.cathodeG, IC1.pin15
  N10: SW1.1, R9.Pin_0, IC2.pin2
  N11: SW1.2, R8.Pin_0, IC2.pin5
  N12: SW1.3, R7.Pin_0, IC2.pin10
  N13: SW1.4, R6.Pin_0, IC2.pin13
  N14: SW1.5, R5.Pin_0, IC2.pin3
  N15: SW1.6, R4.Pin_0, IC2.pin6
  N16: SW1.7, R3.Pin_0, IC2.pin11
  N17: SW1.8, R2.Pin_0, IC2.pin14
  N18: SW1.9, SW1.10, SW1.11, SW1.12, SW1.13, SW1.14, SW1.15, SW1.16, IC1.pin1, IC1.pin10, R1.Pin_1, IC2.pin8, IC2.pin15
  N19: IC1.pin3, X1.2
  N20: IC1.pin4, X1.3
  N21: IC1.pin7, X1.4
  N22: IC1.pin8, X1.5
  N23: IC1.pin11, X1.1
  N24: IC1.pin13, X1.6
  N25: IC1.pin14, X1.7
  N26: IC1.pin17, X1.8
  N27: IC1.pin18, X1.9
  N28: IC1.pin20, R2.Pin_1, R3.Pin_1, R4.Pin_1, R5.Pin_1, R6.Pin_1, R7.Pin_1, R8.Pin_1, R9.Pin_1, IC2.pin16
  N29: X1.11, IC2.pin12
  N30: X1.12, IC2.pin9
  N31: X1.13, IC2.pin7
  N32: X1.15, IC2.pin4
  N33: X1.17, IC2.pin1
